# Fritzing sketch Variable Clock (saved by Fritzing 0.9.3b)
circuit board: 8.46667cm x 5.64444cm
breadboards: 1

parts:
  PIC1 = PIC18F4xK42 [package="DIP (Dual Inline) [THT]"]
  S1 = Pushbutton [package="[THT]"]
  S2 = Pushbutton [package="[THT]"]
  OLED1 = OLED 128x64 I2C Monochrome Display
  R1 = Resistor [tolerance=±5% resistance=10k package=THT]
  R2 = Resistor [tolerance=±5% resistance=10k package=THT]
  C1 = Ceramic Capacitor [capacitance=0.1µF package="200 mil [THT, multilayer]"]
  R3 = Resistor [tolerance=±5% resistance=470 package=THT]
  C2 = Ceramic Capacitor [capacitance=0.1µF package="200 mil [THT, multilayer]"]
  R4 = Resistor [tolerance=±5% resistance=10k package=THT]
  Power_plug1 = Power plug

nets:
  N1: PIC1.VPP/MCLR#/RE3, R3.Pin_1
  N2: PIC1.RA0, S2.Pin_1, S2.Pin_2, R2.Pin_0
  N3: PIC1.RA1, S1.Pin_3, S1.Pin_4, R1.Pin_0
  GND: PIC1.RD6, PIC1.VSS#30, PIC1.RB0, OLED1.GND, OLED1.SCK, R1.Pin_1, R2.Pin_1, C1.0, C2.1, Power_plug1.GND
  VDD: PIC1.RD7, PIC1.VDD#31, PIC1.RB1, S1.Pin_1, S1.Pin_2, S2.Pin_3, S2.Pin_4, OLED1.VDD, OLED1.SDA, C1.1, R4.Pin_0, Power_plug1.VCC
  N4: R3.Pin_0, C2.0, R4.Pin_1

custom parts:
  PIC18F4xK42: The PIC18(L)F26/27/45/46/47/55/56/57K42 microcontrollers are available in 28/40/44/48-pin devices. These devices feature a 12-bit ADC with Computation (ADC2) automating Capacitive Voltage Divider (CVD) techniques for advanced touch sensing, averaging, filtering, oversampling and threshold comparison, Temperature Sensor, Vectored Interrupt Controller with fixed latency for handling interrupts,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
